// Logisim project proj_2_1.circ as structural Verilog: 5 circuits, main circuit testbench
module inst_fetch (
  input  clk,
  input  rst,
  input  control_en_i,
  input  [31:0] control_pc_i,
  input  [15:0] inst_i,
  output inst_en_o,
  output [31:0] current_pc_o,
  output [31:0] inst_addr_o,
  output [15:0] inst_o
);

  wire not_1_out, not_2_out;
  wire [31:0] adder_1_out, counter_1_q, multiplexer_1_out;

  not not_1 (not_1_out, rst);
  Adder #(.width(32)) adder_1 (.a(control_pc_i), .b(32'h1), .out(adder_1_out));  // open: cin, cout
  Counter #(.max('hffffffff), .width(32)) counter_1 (
    .clr(rst), .load(control_en_i), .up(not_1_out), .count(not_1_out), .clk(clk), .D(adder_1_out),
    .Q(counter_1_q));  // open: carry
  Multiplexer #(.width(32)) multiplexer_1 (
    .in0(counter_1_q), .in1(control_pc_i), .out(multiplexer_1_out), .sel(control_en_i));
  not not_2 (not_2_out, rst);
  Register #(.width(32)) register_1 (.D(multiplexer_1_out), .en(not_2_out), .clk(clk), .Q(current_pc_o), .clr(rst));
  not not_3 (inst_en_o, rst);

  assign inst_addr_o = current_pc_o;
  assign inst_o = inst_i;

  // Notes on the sheet:
  //   Don't touch
endmodule

module TOP (
  input  rst,
  input  clk,
  input  [15:0] inst,
  input  [31:0] mem_result,
  input  [31:0] current_pc,
  output mem_wen,
  output [31:0] mem_din,
  output mem_ren,
  output [31:0] alu_result,
  output control_en,
  output [31:0] control_pc,
  output wb_en,
  output [4:0] wb_addr,
  output [31:0] wb_data
);

  wire alu_1_wb_enable, comparator_1_eq, R_0;
  wire [31:0] bit_extender_1_out, multiplexer_1_out, regfile_1_x_rs1, regfile_1_x_rs2;

  Comparator #(.mode("unsigned"), .width(3)) comparator_1 (
    .a(inst[15:13]), .b(3'b100), .eq(comparator_1_eq));  // open: gt, lt
  not not_1 (R_0, comparator_1_eq);
  assign bit_extender_1_out = {{26{inst[12]}}, {inst[12], inst[6:2]}};  // Bit_Extender bit_extender_1
  regfile regfile_1 (
    .x_rd(alu_result), .rs1(inst[11:7]), .rs2(inst[6:2]), .reset(rst), .clk(clk), .write_enable(wb_en),
    .x_rs1(regfile_1_x_rs1), .x_rs2(regfile_1_x_rs2));
  Multiplexer #(.width(32)) multiplexer_1 (
    .in0(regfile_1_x_rs2), .in1(bit_extender_1_out), .out(multiplexer_1_out), .sel(R_0));
  Multiplexer #(.width(32)) multiplexer_2 (.in0(alu_result), .in1({32{1'b0}}), .out(wb_data), .sel(rst));
  ALU alu_1 (
    .rs1(regfile_1_x_rs1), .rs2(multiplexer_1_out), .fun4(inst[15:12]), .opcode(inst[1:0]),
    .alu_result(alu_result), .men_wen(mem_wen), .mem_ren(mem_ren), .control_en(control_en),
    .wb_enable(alu_1_wb_enable));
  Multiplexer multiplexer_3 (.in0(alu_1_wb_enable), .in1(1'b0), .out(wb_en), .sel(rst));
  Multiplexer #(.width(5)) multiplexer_4 (.in0(inst[11:7]), .in1({5{1'b0}}), .out(wb_addr), .sel(rst));

  assign control_pc = alu_result;

  // Other names for the same wires on the sheet: fun3[2:0] = inst[15:13]; fun4[3:0] = inst[15:12];
  //   imm[5:0] = {inst[12], inst[6:2]}; jump[10:0] = inst[12:2]; rs2[4:0] = inst[6:2]; opcode[1:0] = inst[1:0];
  //   rs1[4:0] = inst[11:7]

  // Notes on the sheet:
  //   Fixed I/O
  //   Don't touch
endmodule

module testbench (
  input  rst,
  output mem_wen,
  output [31:0] mem_din,
  output mem_ren,
  output [31:0] alu_result,
  output control_en,
  output [31:0] control_pc,
  output halt,
  output wb_en,
  output [4:0] wb_addr,
  output [31:0] wb_data
);

  wire clk, inst_en, not_1_out, not_2_out, not_3_out, not_4_out, por_1_out, rst_t;
  wire [15:0] inst, inst_i;
  wire [31:0] current_pc, inst_addr, mem_result;

  not not_1 (not_1_out, inst_i[0]);
  not not_2 (not_2_out, inst_i[1]);
  not not_3 (not_3_out, inst_i[13]);
  not not_4 (not_4_out, inst_i[14]);
  and and_1 (halt, not_1_out, not_2_out, not_3_out, not_4_out, inst_i[15]);
  Clock clock_1 (.out(clk));
  or or_1 (rst_t, rst, por_1_out);
  POR por_1 (.out(por_1_out));
  inst_fetch inst_fetch_1 (
    .clk(clk), .rst(rst_t), .control_en_i(control_en), .control_pc_i(control_pc), .inst_i(inst_i),
    .inst_en_o(inst_en), .current_pc_o(current_pc), .inst_addr_o(inst_addr), .inst_o(inst));
  TOP top_1 (
    .rst(rst_t), .clk(clk), .inst(inst), .mem_result(mem_result), .current_pc(current_pc), .mem_wen(mem_wen),
    .mem_din(mem_din), .mem_ren(mem_ren), .alu_result(alu_result), .control_en(control_en),
    .control_pc(control_pc), .wb_en(wb_en), .wb_addr(wb_addr), .wb_data(wb_data));
  ROM #(.dataWidth(16)) rom_1 (.addr(inst_addr[7:0]), .data(inst_i));
  RAM #(.addrWidth(16), .clearpin("true"), .dataWidth(32), .\type ("nonvolatile")) ram_1 (
    .addr(alu_result[15:0]), .we(mem_wen), .oe(mem_ren), .clk(clk), .din(mem_din), .dout(mem_result),
    .clr(rst_t));

  // Notes on the sheet:
  //   contents of rom_1 (hex, n*v repeats v):
  //   4425 6525 40e 942a 84a2 49d 8000 1 1 942a 942a 942a 84a2
  //   you can write any instruction in
endmodule

module regfile (
  input  [31:0] x_rd,
  input  [4:0] rs1,
  input  [4:0] rs2,
  input  reset,
  input  clk,
  input  write_enable,
  output [31:0] x_rs1,
  output [31:0] x_rs2
);

  wire demultiplexer_1_out0, demultiplexer_1_out2, demultiplexer_1_out8, demultiplexer_1_out9,
       demultiplexer_1_out10, demultiplexer_1_out11, demultiplexer_1_out12, demultiplexer_1_out13,
       demultiplexer_1_out14, demultiplexer_1_out15, or_1_out, or_2_out, or_3_out, or_4_out, or_5_out,
       or_6_out, or_7_out, or_8_out, or_9_out, or_10_out;
  wire [31:0] x0, x2, x8, x9, x10, x11, x12, x13, x14, x15;

  Demultiplexer #(.select(5)) demultiplexer_1 (
    .out0(demultiplexer_1_out0), .out2(demultiplexer_1_out2), .out8(demultiplexer_1_out8),
    .out9(demultiplexer_1_out9), .out10(demultiplexer_1_out10), .out11(demultiplexer_1_out11),
    .out12(demultiplexer_1_out12), .out13(demultiplexer_1_out13), .out14(demultiplexer_1_out14),
    .out15(demultiplexer_1_out15), .in(write_enable), .sel(rs1));  // open: out1, out3, out4, out5, out6, out7, out16, out17, out18, out19, out20, out21, out22, out23, out24, out25, out26, out27, out28, out29, out30, out31
  or or_1 (or_1_out, reset, demultiplexer_1_out0);
  or or_2 (or_2_out, reset, demultiplexer_1_out2);
  or or_3 (or_3_out, reset, demultiplexer_1_out8);
  or or_4 (or_4_out, reset, demultiplexer_1_out9);
  or or_5 (or_5_out, reset, demultiplexer_1_out10);
  or or_6 (or_6_out, reset, demultiplexer_1_out11);
  or or_7 (or_7_out, reset, demultiplexer_1_out12);
  or or_8 (or_8_out, reset, demultiplexer_1_out13);
  or or_9 (or_9_out, reset, demultiplexer_1_out14);
  or or_10 (or_10_out, reset, demultiplexer_1_out15);
  Register #(.width(32)) register_1 (.D(x_rd), .en(or_1_out), .clk(clk), .Q(x0), .clr(reset));
  Register #(.width(32)) register_2 (.D(x_rd), .en(or_2_out), .clk(clk), .Q(x2), .clr(reset));
  Register #(.width(32)) register_3 (.D(x_rd), .en(or_3_out), .clk(clk), .Q(x8), .clr(reset));
  Register #(.width(32)) register_4 (.D(x_rd), .en(or_4_out), .clk(clk), .Q(x9), .clr(reset));
  Register #(.width(32)) register_5 (.D(x_rd), .en(or_5_out), .clk(clk), .Q(x10), .clr(reset));
  Register #(.width(32)) register_6 (.D(x_rd), .en(or_6_out), .clk(clk), .Q(x11), .clr(reset));
  Register #(.width(32)) register_7 (.D(x_rd), .en(or_7_out), .clk(clk), .Q(x12), .clr(reset));
  Register #(.width(32)) register_8 (.D(x_rd), .en(or_8_out), .clk(clk), .Q(x13), .clr(reset));
  Register #(.width(32)) register_9 (.D(x_rd), .en(or_9_out), .clk(clk), .Q(x14), .clr(reset));
  Register #(.width(32)) register_10 (.D(x_rd), .en(or_10_out), .clk(clk), .Q(x15), .clr(reset));
  Multiplexer #(.select(5), .width(32)) multiplexer_1 (
    .in0(x0), .in2(x2), .in8(x8), .in9(x9), .in10(x10), .in11(x11), .in12(x12), .in13(x13), .in14(x14),
    .in15(x15), .out(x_rs1), .sel(rs1));  // open: in1, in3, in4, in5, in6, in7, in16, in17, in18, in19, in20, in21, in22, in23, in24, in25, in26, in27, in28, in29, in30, in31
  Multiplexer #(.select(5), .width(32)) multiplexer_2 (
    .in0(x0), .in2(x2), .in8(x8), .in9(x9), .in10(x10), .in11(x11), .in12(x12), .in13(x13), .in14(x14),
    .in15(x15), .out(x_rs2), .sel(rs2));  // open: in1, in3, in4, in5, in6, in7, in16, in17, in18, in19, in20, in21, in22, in23, in24, in25, in26, in27, in28, in29, in30, in31

  // Other names for the same wires on the sheet: writeen = write_enable
endmodule

module ALU (
  input  [31:0] rs1,
  input  [31:0] rs2,
  input  [3:0] fun4,
  input  [1:0] opcode,
  output [31:0] alu_result,
  output men_wen,
  output mem_ren,
  output control_en,
  output wb_enable
);

  wire comparator_1_eq;
  wire [31:0] add, lui, slli;
  wire [35:0] multiplexer_1_out, multiplexer_2_out;
  wire [35:35] multiplexer_3_out;

  Multiplexer #(.select(4), .width(36)) multiplexer_1 (
    .in0({4'b1000, slli}), .in1({4'b1000, slli}), .in8({4'b1000, rs2}), .in9({4'b1000, add}),
    .out(multiplexer_1_out), .sel(fun4));  // open: in2, in3, in4, in5, in6, in7, in10, in11, in12, in13, in14, in15
  Multiplexer #(.select(4), .width(36)) multiplexer_2 (
    .in0({4'b1000, add}), .in1({4'b1000, add}), .in4({4'b1000, rs2}), .in5({4'b1000, rs2}),
    .in6({4'b1000, lui}), .in7({4'b1000, lui}), .in8({4'b1000, rs2}), .in9({4'b1000, add}),
    .out(multiplexer_2_out), .sel(fun4));  // open: in2, in3, in10, in11, in12, in13, in14, in15
  Multiplexer #(.select(2), .width(36)) multiplexer_3 (
    .in0(multiplexer_2_out), .in1(multiplexer_2_out), .in2(multiplexer_1_out), .in3(multiplexer_1_out),
    .out({multiplexer_3_out[35], control_en, mem_ren, men_wen, alu_result}), .sel(opcode));
  Shifter #(.width(32)) shifter_1 (.in(rs2), .\dist (5'b01100), .out(lui));
  Comparator #(.mode("unsigned"), .width(6)) comparator_1 (
    .a({fun4, opcode}), .b(6'b100000), .eq(comparator_1_eq));  // open: gt, lt
  Multiplexer multiplexer_4 (.in0(multiplexer_3_out[35]), .in1(1'b0), .out(wb_enable), .sel(comparator_1_eq));
  Adder #(.width(32)) adder_1 (.a(rs1), .b(rs2), .out(add));  // open: cin, cout
  Shifter #(.width(32)) shifter_2 (.in(rs1), .\dist (rs2[4:0]), .out(slli));

  // Other names for the same wires on the sheet: result[31:0] = alu_result; ctro_enable = control_en;
  //   addi[31:0] = add; li[31:0] = rs2; mv[31:0] = rs2
endmodule
