// Logisim project proj_2_2.circ as structural Verilog: 5 circuits, main circuit testbench
module inst_fetch (
  input  clk,
  input  rst,
  input  control_en_i,
  input  [31:0] control_pc_i,
  input  [15:0] inst_i,
  output inst_en_o,
  output [31:0] current_pc_o,
  output [31:0] inst_addr_o,
  output [15:0] inst_o
);

  wire not_1_out, not_2_out;
  wire [31:0] adder_1_out, counter_1_q, multiplexer_1_out;

  not not_1 (not_1_out, rst);
  Adder #(.width(32)) adder_1 (.a(control_pc_i), .b(32'h1), .out(adder_1_out));  // open: cin, cout
  Counter #(.max('hffffffff), .width(32)) counter_1 (
    .clr(rst), .load(control_en_i), .up(not_1_out), .count(not_1_out), .clk(clk), .D(adder_1_out),
    .Q(counter_1_q));  // open: carry
  Multiplexer #(.width(32)) multiplexer_1 (
    .in0(counter_1_q), .in1(control_pc_i), .out(multiplexer_1_out), .sel(control_en_i));
  not not_2 (not_2_out, rst);
  Register #(.width(32)) register_1 (.D(multiplexer_1_out), .en(not_2_out), .clk(clk), .Q(current_pc_o), .clr(rst));
  not not_3 (inst_en_o, rst);

  assign inst_addr_o = current_pc_o;
  assign inst_o = inst_i;

  // Notes on the sheet:
  //   Don't touch
endmodule

module TOP (
  input  rst,
  input  clk,
  input  [15:0] inst,
  input  [31:0] mem_result,
  input  [31:0] current_pc,
  output mem_wen,
  output [31:0] mem_din,
  output mem_ren,
  output [31:0] alu_result,
  output control_en,
  output [31:0] control_pc,
  output wb_en,
  output [4:0] wb_addr,
  output [31:0] wb_data,
  output [31:0] out_15,
  output [31:0] out_16
);

  wire addi4spn, alu_1_wb_enable, and_3_out, and_5_out, comparator_1_eq, comparator_2_eq, comparator_3_eq,
       comparator_4_eq, comparator_5_eq, comparator_6_eq, comparator_7_lt, comparator_8_eq, comparator_9_eq,
       comparator_10_eq, comparator_11_eq, comparator_12_eq, comparator_13_eq, comparator_14_eq,
       comparator_15_eq, lw, multiplexer_10_out, nor_1_out, or_1_out, or_2_out, or_3_out, or_4_out, R_0, sw,
       swsp;
  wire [4:0] adder_1_out, adder_2_out, adder_3_out, bit_extender_2_out, bit_extender_3_out,
       bit_extender_4_out, multiplexer_1_out, multiplexer_11_out, multiplexer_14_out, rd, real_rs1, real_rs2;
  wire [31:0] alu_1_alu_result, bit_extender_1_out, multiplexer_2_out, multiplexer_4_out, regfile_1_x_rs2;

  Comparator #(.width(2)) comparator_1 (.a(inst[1:0]), .b(2'b10), .eq(comparator_1_eq));  // open: gt, lt
  Comparator #(.width(3)) comparator_2 (.a(inst[15:13]), .b(3'b110), .eq(comparator_2_eq));  // open: gt, lt
  Comparator #(.width(2)) comparator_3 (.a(inst[1:0]), .b(2'b00), .eq(comparator_3_eq));  // open: gt, lt
  Comparator #(.width(3)) comparator_4 (.a(inst[15:13]), .b(3'b000), .eq(comparator_4_eq));  // open: gt, lt
  Comparator #(.mode("unsigned"), .width(3)) comparator_5 (
    .a(inst[15:13]), .b(3'b100), .eq(comparator_5_eq));  // open: gt, lt
  Multiplexer #(.width(5)) multiplexer_1 (.in0(inst[11:7]), .in1(5'b00010), .out(multiplexer_1_out), .sel(or_1_out));
  and and_1 (swsp, comparator_1_eq, comparator_2_eq);
  and and_2 (addi4spn, comparator_3_eq, comparator_4_eq);
  not not_1 (R_0, comparator_5_eq);
  Comparator #(.width(2)) comparator_6 (.a(inst[1:0]), .b(2'b00), .eq(comparator_6_eq));  // open: gt, lt
  Comparator #(.mode("unsigned"), .width(3)) comparator_7 (
    .a(inst[15:13]), .b(3'b110), .lt(comparator_7_lt));  // open: gt, eq
  or or_1 (or_1_out, swsp, addi4spn);
  Multiplexer #(.width(32)) multiplexer_2 (.in0(alu_result), .in1(mem_result), .out(multiplexer_2_out), .sel(lw));
  assign bit_extender_1_out = {{21{inst[12]}}, inst[12:2]};  // Bit_Extender bit_extender_1
  assign bit_extender_2_out = {{2{1'b0}}, inst[4:2]};  // Bit_Extender bit_extender_2
  Multiplexer #(.width(5)) multiplexer_3 (.in0(inst[11:7]), .in1(adder_1_out), .out(rd), .sel(and_3_out));
  Adder #(.width(5)) adder_1 (.a(bit_extender_2_out), .b(5'b01000), .out(adder_1_out));  // open: cin, cout
  and and_3 (and_3_out, comparator_6_eq, comparator_7_lt);
  assign bit_extender_3_out = {{2{1'b0}}, inst[9:7]};  // Bit_Extender bit_extender_3
  Comparator #(.width(2)) comparator_8 (.a(inst[1:0]), .b(2'b00), .eq(comparator_8_eq));  // open: gt, lt
  Comparator #(.width(3)) comparator_9 (.a(inst[15:13]), .b(3'b110), .eq(comparator_9_eq));  // open: gt, lt
  Comparator #(.width(2)) comparator_10 (.a(inst[1:0]), .b(2'b01), .eq(comparator_10_eq));  // open: gt, lt
  Comparator #(.width(3)) comparator_11 (.a(inst[15:13]), .b(3'b110), .eq(comparator_11_eq));  // open: gt, lt
  Comparator #(.width(2)) comparator_12 (.a(inst[1:0]), .b(2'b00), .eq(comparator_12_eq));  // open: gt, lt
  Comparator #(.width(3)) comparator_13 (.a(inst[15:13]), .b(3'b010), .eq(comparator_13_eq));  // open: gt, lt
  Multiplexer #(.width(32)) multiplexer_4 (.in0(alu_result), .in1({32{1'b0}}), .out(multiplexer_4_out), .sel(rst));
  Adder #(.width(5)) adder_2 (.a(bit_extender_3_out), .b(5'b01000), .out(adder_2_out));  // open: cin, cout
  and and_4 (sw, comparator_8_eq, comparator_9_eq);
  and and_5 (and_5_out, comparator_10_eq, comparator_11_eq);
  and and_6 (lw, comparator_12_eq, comparator_13_eq);
  Multiplexer #(.width(5)) multiplexer_5 (.in0(multiplexer_1_out), .in1(adder_2_out), .out(real_rs1), .sel(or_3_out));
  regfile regfile_1 (
    .x_rd(multiplexer_2_out), .rd(rd), .rs1(real_rs1), .rs2(real_rs2), .reset(rst), .clk(clk),
    .write_enable(wb_en), .x_rs1(out_15), .x_rs2(regfile_1_x_rs2));
  or or_2 (or_2_out, sw, and_5_out);
  Multiplexer #(.width(32)) multiplexer_6 (.in0(regfile_1_x_rs2), .in1(bit_extender_1_out), .out(out_16), .sel(R_0));
  Multiplexer #(.width(32)) multiplexer_7 (.in0(multiplexer_4_out), .in1(mem_result), .out(wb_data), .sel(lw));
  or or_3 (or_3_out, or_2_out, lw);
  Multiplexer #(.width(32)) multiplexer_8 (.in0(alu_result), .in1({32{1'b0}}), .out(control_pc), .sel(rst));
  ALU alu_1 (
    .rs1(out_15), .rs2(out_16), .fun4(inst[15:12]), .opcode(inst[1:0]), .current_pc(current_pc),
    .alu_result(alu_1_alu_result), .men_wen(mem_wen), .mem_ren(mem_ren), .control_en(control_en),
    .wb_enable(alu_1_wb_enable));
  assign bit_extender_4_out = {{2{1'b0}}, inst[4:2]};  // Bit_Extender bit_extender_4
  Multiplexer #(.width(32)) multiplexer_9 (.in0(regfile_1_x_rs2), .in1({32{1'b0}}), .out(mem_din), .sel(or_4_out));
  Multiplexer multiplexer_10 (.in0(alu_1_wb_enable), .in1(1'b0), .out(multiplexer_10_out), .sel(rst));
  Multiplexer #(.width(5)) multiplexer_11 (.in0(rd), .in1({5{1'b0}}), .out(multiplexer_11_out), .sel(rst));
  Comparator #(.width(5)) comparator_14 (
    .a(5'b10101), .b({inst[15:13], inst[1:0]}), .eq(comparator_14_eq));  // open: gt, lt
  Adder #(.width(5)) adder_3 (.a(bit_extender_4_out), .b(5'b01000), .out(adder_3_out));  // open: cin, cout
  or or_4 (or_4_out, rst, nor_1_out);
  Multiplexer #(.width(32)) multiplexer_12 (.in0(alu_1_alu_result), .in1({32{1'b0}}), .out(alu_result), .sel(rst));
  Multiplexer #(.width(5)) multiplexer_13 (.in0(inst[6:2]), .in1(adder_3_out), .out(real_rs2), .sel(sw));
  nor nor_1 (nor_1_out, swsp, sw);
  Comparator #(.width(5)) comparator_15 (.a({5{1'b0}}), .b(rd), .eq(comparator_15_eq));  // open: gt, lt
  Multiplexer #(.width(5)) multiplexer_14 (
    .in0(multiplexer_11_out), .in1({5{1'b0}}), .out(multiplexer_14_out), .sel(comparator_14_eq));
  Comparator #(.width(3)) comparator_16 ();  // open: a, b, gt, eq, lt
  Multiplexer multiplexer_15 (.in0(multiplexer_10_out), .in1(1'b0), .out(wb_en), .sel(comparator_15_eq));
  Multiplexer #(.width(5)) multiplexer_16 (.in0({5{1'b0}}), .in1(multiplexer_14_out), .out(wb_addr), .sel(wb_en));

  // Other names for the same wires on the sheet: opcode[1:0] = inst[1:0]; fun3[2:0] = inst[15:13];
  //   fun4[3:0] = inst[15:12]; imm[5:0] = {inst[12], inst[6:2]}; imm2[10:0] = inst[12:2]; jump[10:0] = inst[12:2];
  //   rd_o[2:0] = inst[4:2]; rs2[4:0] = inst[6:2]; rs1[4:0] = inst[11:7]; rs1_o[2:0] = inst[9:7]

  // Notes on the sheet:
  //   Fixed I/O
  //   Don't touch
endmodule

module testbench (
  input  rst,
  output mem_wen,
  output [31:0] mem_din,
  output mem_ren,
  output [31:0] mem_addr,
  output control_en,
  output [31:0] control_pc,
  output halt,
  output wb_en,
  output [4:0] wb_addr,
  output [31:0] wb_data
);

  wire clk, inst_en, not_1_out, not_2_out, not_3_out, not_4_out, por_1_out, rst_t;
  wire [15:0] inst, inst_i;
  wire [31:0] current_pc, inst_addr, mem_result;

  not not_1 (not_1_out, inst_i[0]);
  not not_2 (not_2_out, inst_i[1]);
  not not_3 (not_3_out, inst_i[13]);
  not not_4 (not_4_out, inst_i[14]);
  and and_1 (halt, not_1_out, not_2_out, not_3_out, not_4_out, inst_i[15]);
  Clock clock_1 (.out(clk));
  or or_1 (rst_t, rst, por_1_out);
  POR por_1 (.out(por_1_out));
  inst_fetch inst_fetch_1 (
    .clk(clk), .rst(rst_t), .control_en_i(control_en), .control_pc_i(control_pc), .inst_i(inst_i),
    .inst_en_o(inst_en), .current_pc_o(current_pc), .inst_addr_o(inst_addr), .inst_o(inst));
  TOP top_1 (
    .rst(rst_t), .clk(clk), .inst(inst), .mem_result(mem_result), .current_pc(current_pc), .mem_wen(mem_wen),
    .mem_din(mem_din), .mem_ren(mem_ren), .alu_result(mem_addr), .control_en(control_en),
    .control_pc(control_pc), .wb_en(wb_en), .wb_addr(wb_addr), .wb_data(wb_data));  // open: out_15, out_16
  ROM #(.dataWidth(16)) rom_1 (.addr(inst_addr[7:0]), .data(inst_i));
  RAM #(.addrWidth(16), .asyncread("true"), .clearpin("true"), .dataWidth(32), .\type ("nonvolatile")) ram_1 (
    .addr(mem_addr[15:0]), .we(mem_wen), .oe(mem_ren), .clk(clk), .din(mem_din), .dout(mem_result),
    .clr(rst_t));

  // Notes on the sheet:
  //   contents of rom_1 (hex, n*v repeats v):
  //   4409 147d c011 bffd 1 1 4111 5429 c422 44b5 48 8482 8526 414c 511 c148 8000
  //   you can write any instruction in
endmodule

module ALU (
  input  [31:0] rs1,
  input  [31:0] rs2,
  input  [3:0] fun4,
  input  [1:0] opcode,
  input  [31:0] current_pc,
  output [31:0] alu_result,
  output men_wen,
  output mem_ren,
  output control_en,
  output wb_enable
);

  wire and_1_out, comparator_2_eq, comparator_3_eq, comparator_4_eq, comparator_5_eq, comparator_6_eq,
       comparator_7_eq, eight, nand_1_out, not_1_out, or_1_out, or_2_out;
  wire [31:0] add, addi, addi4spn, bit_extender_1_out, bit_extender_2_out, bit_extender_4_out,
       bit_extender_5_out, bit_extender_6_out, bit_extender_7_out, bit_extender_8_out, j, li, lw, slli, swsp;
  wire [34:0] beqz;
  wire [36:0] lui, multiplexer_1_out, multiplexer_2_out;
  wire [36:35] multiplexer_3_out;

  Multiplexer #(.select(5), .width(37)) multiplexer_1 (
    .in0({5'b11000, addi4spn}), .in1({5'b11000, addi}), .in2({5'b11000, slli}), .in8({5'b11010, lw}),
    .in9({5'b11000, li}), .in13({lui[36], 4'b1000, lui[31:0]}), .in16({37{1'b0}}), .in18({5'b11000, add}),
    .in21({5'b10100, j}), .in24({5'b10001, lw}), .in25({2'b10, beqz[34], 2'b00, beqz[31:0]}),
    .in26({5'b10001, swsp}), .out(multiplexer_1_out), .sel({fun4[3:1], opcode}));  // open: in3, in4, in5, in6, in7, in10, in11, in12, in14, in15, in17, in19, in20, in22, in23, in27, in28, in29, in30, in31
  Comparator #(.width(37)) comparator_1 (.a({37{1'b0}}), .b(multiplexer_1_out), .eq(eight));  // open: gt, lt
  Comparator #(.width(4)) comparator_2 (.a(4'b1000), .b(fun4), .eq(comparator_2_eq));  // open: gt, lt
  Multiplexer #(.width(37)) multiplexer_2 (
    .in0({5'b11000, rs2}), .in1(multiplexer_1_out), .out(multiplexer_2_out), .sel(or_1_out));
  or or_1 (or_1_out, eight, not_1_out);
  not not_1 (not_1_out, and_1_out);
  and and_1 (and_1_out, comparator_2_eq, comparator_3_eq);
  Comparator #(.width(2)) comparator_3 (.a(opcode), .b(2'b10), .eq(comparator_3_eq));  // open: gt, lt
  Comparator #(.width(5)) comparator_4 (.a({5{1'b0}}), .b(rs2[4:0]), .eq(comparator_4_eq));  // open: gt, lt
  Comparator #(.width(2)) comparator_5 (.a(opcode), .b(2'b10), .eq(comparator_5_eq));  // open: gt, lt
  Comparator #(.width(4)) comparator_6 (.a(4'b1000), .b(fun4), .eq(comparator_6_eq));  // open: gt, lt
  assign bit_extender_1_out = {{20{rs2[10]}}, {rs2[10], rs2[6], rs2[8:7], rs2[4], rs2[5], rs2[0], rs2[9], rs2[3:1], 1'b0}};  // Bit_Extender bit_extender_1
  Multiplexer #(.width(37)) multiplexer_3 (
    .in0({5'b10100, rs1}), .in1(multiplexer_2_out),
    .out({multiplexer_3_out, control_en, mem_ren, men_wen, alu_result}), .sel(or_2_out));
  or or_2 (or_2_out, nand_1_out, eight);
  nand nand_1 (nand_1_out, comparator_4_eq, comparator_5_eq, comparator_6_eq);
  assign bit_extender_2_out = {{26{rs2[10]}}, {rs2[10], rs2[4:0]}};  // Bit_Extender bit_extender_2
  Shifter #(.width(32)) shifter_1 (.in(bit_extender_2_out), .\dist (5'b01100), .out(lui[31:0]));
  assign li = {{26{rs2[10]}}, {rs2[10], rs2[4:0]}};  // Bit_Extender bit_extender_3
  Adder #(.width(32)) adder_1 (.a(bit_extender_1_out), .b(current_pc), .out(j));  // open: cin, cout
  Adder #(.width(32)) adder_2 (.a(rs1), .b(rs2), .out(add));  // open: cin, cout
  Comparator #(.width(6)) comparator_7 (.a({fun4, opcode}), .b(6'b100000), .eq(comparator_7_eq));  // open: gt, lt
  Shifter #(.width(32)) shifter_2 (.in(rs1), .\dist (rs2[4:0]), .out(slli));
  assign bit_extender_4_out = {{24{1'b0}}, {rs2[6:5], rs2[10:7], 2'b00}};  // Bit_Extender bit_extender_4
  assign bit_extender_5_out = {{23{rs2[10]}}, {rs2[10], rs2[4:3], rs2[0], rs2[9:8], rs2[2:1], 1'b0}};  // Bit_Extender bit_extender_5
  Multiplexer multiplexer_4 (.in0(multiplexer_3_out[35]), .in1(1'b0), .out(wb_enable), .sel(comparator_7_eq));
  Adder #(.width(32)) adder_3 (.a(rs1), .b(bit_extender_4_out), .out(swsp));  // open: cin, cout
  assign bit_extender_6_out = {{25{1'b0}}, {rs2[3], rs2[10:8], rs2[4], 2'b00}};  // Bit_Extender bit_extender_6
  Comparator #(.width(32)) comparator_8 (.a(rs1), .b({32{1'b0}}), .eq(beqz[34]));  // open: gt, lt
  Adder #(.width(32)) adder_4 (.a(current_pc), .b(bit_extender_5_out), .out(beqz[31:0]));  // open: cin, cout
  Adder #(.width(32)) adder_5 (.a(rs1), .b(bit_extender_6_out), .out(lw));  // open: cin, cout
  assign bit_extender_7_out = {{26{rs2[10]}}, {rs2[10], rs2[4:0]}};  // Bit_Extender bit_extender_7
  assign bit_extender_8_out = {{22{1'b0}}, {rs2[8:5], rs2[10:9], rs2[3], rs2[4], 2'b00}};  // Bit_Extender bit_extender_8
  Adder #(.width(32)) adder_6 (.a(rs1), .b(bit_extender_7_out), .out(addi));  // open: cin, cout
  Adder #(.width(32)) adder_7 (.a(rs1), .b(bit_extender_8_out), .out(addi4spn));  // open: cin, cout

  // Other names for the same wires on the sheet: result[31:0] = alu_result; ctro_enable = control_en;
  //   fun4th = fun4[0]; fun3[2:0] = fun4[3:1]; beqz_imm[7:0] = {rs2[10:8], rs2[4:0]};
  //   beqz_off[8:1] = {rs2[10], rs2[4:3], rs2[0], rs2[9:8], rs2[2:1]}; imm[10:0] = rs2[10:0]; imm1[2:0] = rs2[2:0];
  //   imm_addi[5:0] = {rs2[10], rs2[4:0]};
  //   j_off[11:1] = {rs2[10], rs2[6], rs2[8:7], rs2[4], rs2[5], rs2[0], rs2[9], rs2[3:1]}; mv[31:0] = rs2;
  //   R_rs2[4:0] = rs2[4:0]; addi4spn_imm[7:0] = rs2[10:3]; addi4spn_off[9:2] = {rs2[8:5], rs2[10:9], rs2[3], rs2[4]};
  //   imm2[1:0] = rs2[4:3]; lw_imm[4:0] = {rs2[10:8], rs2[4:3]}; lw_off[6:2] = {rs2[3], rs2[10:8], rs2[4]};
  //   sw_imm[4:0] = {rs2[10:8], rs2[4:3]}; sw_off[6:2] = {rs2[3], rs2[10:8], rs2[4]}; imm4[1:0] = rs2[9:8];
  //   swsp_imm[5:0] = rs2[10:5]; swsp_off[7:2] = {rs2[6:5], rs2[10:7]}; imm3[2:0] = rs2[7:5]; imm5 = rs2[10];
  //   jr[31:0] = rs1; sw[31:0] = lw
endmodule

module regfile (
  input  [31:0] x_rd,
  input  [4:0] rd,
  input  [4:0] rs1,
  input  [4:0] rs2,
  input  reset,
  input  clk,
  input  write_enable,
  output [31:0] x_rs1,
  output [31:0] x_rs2
);

  wire demultiplexer_1_out0, demultiplexer_1_out2, demultiplexer_1_out8, demultiplexer_1_out9,
       demultiplexer_1_out10, demultiplexer_1_out11, demultiplexer_1_out12, demultiplexer_1_out13,
       demultiplexer_1_out14, demultiplexer_1_out15, or_1_out, or_2_out, or_3_out, or_4_out, or_5_out,
       or_6_out, or_7_out, or_8_out, or_9_out, or_10_out;
  wire [31:0] x0, x2, x8, x9, x10, x11, x12, x13, x14, x15;

  Demultiplexer #(.select(5)) demultiplexer_1 (
    .out0(demultiplexer_1_out0), .out2(demultiplexer_1_out2), .out8(demultiplexer_1_out8),
    .out9(demultiplexer_1_out9), .out10(demultiplexer_1_out10), .out11(demultiplexer_1_out11),
    .out12(demultiplexer_1_out12), .out13(demultiplexer_1_out13), .out14(demultiplexer_1_out14),
    .out15(demultiplexer_1_out15), .in(write_enable), .sel(rd));  // open: out1, out3, out4, out5, out6, out7, out16, out17, out18, out19, out20, out21, out22, out23, out24, out25, out26, out27, out28, out29, out30, out31
  or or_1 (or_1_out, reset, demultiplexer_1_out0);
  or or_2 (or_2_out, reset, demultiplexer_1_out2);
  or or_3 (or_3_out, reset, demultiplexer_1_out8);
  or or_4 (or_4_out, reset, demultiplexer_1_out9);
  or or_5 (or_5_out, reset, demultiplexer_1_out10);
  or or_6 (or_6_out, reset, demultiplexer_1_out11);
  or or_7 (or_7_out, reset, demultiplexer_1_out12);
  or or_8 (or_8_out, reset, demultiplexer_1_out13);
  or or_9 (or_9_out, reset, demultiplexer_1_out14);
  or or_10 (or_10_out, reset, demultiplexer_1_out15);
  Register #(.width(32)) register_1 (.D({32{1'b0}}), .en(or_1_out), .clk(clk), .Q(x0), .clr(reset));
  Register #(.width(32)) register_2 (.D(x_rd), .en(or_2_out), .clk(clk), .Q(x2), .clr(reset));
  Register #(.width(32)) register_3 (.D(x_rd), .en(or_3_out), .clk(clk), .Q(x8), .clr(reset));
  Register #(.width(32)) register_4 (.D(x_rd), .en(or_4_out), .clk(clk), .Q(x9), .clr(reset));
  Register #(.width(32)) register_5 (.D(x_rd), .en(or_5_out), .clk(clk), .Q(x10), .clr(reset));
  Register #(.width(32)) register_6 (.D(x_rd), .en(or_6_out), .clk(clk), .Q(x11), .clr(reset));
  Register #(.width(32)) register_7 (.D(x_rd), .en(or_7_out), .clk(clk), .Q(x12), .clr(reset));
  Register #(.width(32)) register_8 (.D(x_rd), .en(or_8_out), .clk(clk), .Q(x13), .clr(reset));
  Register #(.width(32)) register_9 (.D(x_rd), .en(or_9_out), .clk(clk), .Q(x14), .clr(reset));
  Register #(.width(32)) register_10 (.D(x_rd), .en(or_10_out), .clk(clk), .Q(x15), .clr(reset));
  Multiplexer #(.select(5), .width(32)) multiplexer_1 (
    .in0(x0), .in2(x2), .in8(x8), .in9(x9), .in10(x10), .in11(x11), .in12(x12), .in13(x13), .in14(x14),
    .in15(x15), .out(x_rs1), .sel(rs1));  // open: in1, in3, in4, in5, in6, in7, in16, in17, in18, in19, in20, in21, in22, in23, in24, in25, in26, in27, in28, in29, in30, in31
  Multiplexer #(.select(5), .width(32)) multiplexer_2 (
    .in0(x0), .in2(x2), .in8(x8), .in9(x9), .in10(x10), .in11(x11), .in12(x12), .in13(x13), .in14(x14),
    .in15(x15), .out(x_rs2), .sel(rs2));  // open: in1, in3, in4, in5, in6, in7, in16, in17, in18, in19, in20, in21, in22, in23, in24, in25, in26, in27, in28, in29, in30, in31

  // Other names for the same wires on the sheet: writeen = write_enable
endmodule
